// Digital circuit part_c.dig as structural Verilog
module part_c (
  input  in_0,
  input  in_1,
  input  in_2,
  output out_0
);

  wire fgpfet_1_d, fgpfet_2_d, fgpfet_3_d, fgpfet_6_d, fgpfet_7_d, nfet_1_d, nfet_3_s, nfet_7_d;

  NFET nfet_1 (.G(in_0), .D(nfet_1_d), .S(1'b0));
  FGPFET fgpfet_1 (.G(in_0), .S(1'b1), .D(fgpfet_1_d));
  FGPFET fgpfet_2 (.G(in_0), .S(1'b1), .D(fgpfet_2_d));
  FGPFET fgpfet_3 (.G(in_1), .S(fgpfet_2_d), .D(fgpfet_3_d));
  FGPFET fgpfet_4 (.G(in_2), .S(fgpfet_3_d), .D(nfet_1_d));
  NFET nfet_2 (.G(in_1), .D(nfet_1_d), .S(1'b0));
  FGPFET fgpfet_5 (.G(in_1), .S(1'b1), .D(fgpfet_1_d));
  NFET nfet_3 (.G(in_0), .D(fgpfet_1_d), .S(nfet_3_s));
  NFET nfet_4 (.G(in_1), .D(nfet_3_s), .S(1'b0));
  NFET nfet_5 (.G(in_2), .D(nfet_1_d), .S(1'b0));
  FGPFET fgpfet_6 (.G(fgpfet_1_d), .S(1'b1), .D(fgpfet_6_d));
  NFET nfet_6 (.G(fgpfet_1_d), .D(fgpfet_6_d), .S(1'b0));
  NFET nfet_7 (.G(nfet_1_d), .D(nfet_7_d), .S(1'b0));
  FGPFET fgpfet_7 (.G(nfet_1_d), .S(1'b1), .D(fgpfet_7_d));
  FGPFET fgpfet_8 (.G(fgpfet_6_d), .S(fgpfet_7_d), .D(nfet_7_d));
  NFET nfet_8 (.G(fgpfet_6_d), .D(nfet_7_d), .S(1'b0));
  FGPFET fgpfet_9 (.G(nfet_7_d), .S(1'b1), .D(out_0));
  NFET nfet_9 (.G(nfet_7_d), .D(out_0), .S(1'b0));
endmodule
